# Fritzing sketch DHT_DISPLAY (saved by Fritzing 0.9.3b)
breadboards: 1

parts:
  Part1 = Arduino Uno (Rev3)
  S1 = Pushbutton [package="[THT]"]
  S2 = Pushbutton [package="[THT]"]
  DHT1 = DHT11 Humitidy and Temperature Sensor (3 pins)
  J1 = Buzzer
  7_Segment_4_Digit_Display1 = 7-SEGMENT-4DIGIT common anode [part_number="5461BS - 5462BS" package=7-segment-4digit-anode]
  R1 = Resistor [tolerance=±5% resistance=1k package=THT]
  R2 = Resistor [tolerance=±5% resistance=1k package=THT]
  R3 = Resistor [tolerance=±5% resistance=1k package=THT]
  R4 = Resistor [tolerance=±5% resistance=1k package=THT]

nets:
  N1: Part1.A2, J1.pin1
  N2: Part1.A3, 7_Segment_4_Digit_Display1.pin_11
  N3: Part1.A4/SDA, 7_Segment_4_Digit_Display1.pin_7
  N4: Part1.D8, 7_Segment_4_Digit_Display1.pin_5
  N5: Part1.D9_PWM, DHT1.Gnd
  N6: Part1.D10_PWM/SS, R4.Pin_0
  N7: Part1.D11_PWM/MOSI, R3.Pin_0
  N8: Part1.D12/MISO, R2.Pin_0
  N9: Part1.D13/SCK, R1.Pin_0
  N10: Part1.GND, S1.Pin_3, S1.Pin_4, DHT1.Plus, J1.pin2
  N11: Part1.D2, S1.Pin_1, S1.Pin_2
  N12: Part1.D3_PWM, S2.Pin_1, S2.Pin_2
  N13: Part1.D4, 7_Segment_4_Digit_Display1.pin_4
  N14: Part1.D5_PWM, 7_Segment_4_Digit_Display1.pin_2
  N15: Part1.D6_PWM, 7_Segment_4_Digit_Display1.pin_1
  N16: Part1.D7, 7_Segment_4_Digit_Display1.pin_10
  N17: Part1.5V, S2.Pin_3, S2.Pin_4, DHT1.Signal
  N18: 7_Segment_4_Digit_Display1.pin_6, R4.Pin_1
  N19: 7_Segment_4_Digit_Display1.pin_8, R3.Pin_1
  N20: 7_Segment_4_Digit_Display1.pin_9, R2.Pin_1
  N21: 7_Segment_4_Digit_Display1.pin_12, R1.Pin_1

custom parts:
  DHT11 Humitidy and Temperature Sensor (3 pins): DHT11 Humidity and Temperature Sensor (3 pins).
  Buzzer: Fixed frequency buzzer
  7-SEGMENT-4DIGIT common anode: A 7 Segment 4 Digit common anode display, with decimal points
